# Fritzing sketch PowerOnGuard (saved by Fritzing 0.9.3b)
breadboards: 1

parts:
  Arduino_Nano = Arduino Nano (Rev3.0) (ICSP)
  SSR = RELAY-SOLIDSTATE [package=relay-s108t02]
  durationExtensionPot_(0-300s) = TRIMPOT [part_number=durationExtensionPoti package=trimpot_pth_s3_lock]
  ampsThresholdPoti_(0-30A) = TRIMPOT [part_number=ampsThresholdPoti package=trimpot_pth_s3_lock]
  maxDurationPoti_(0-1h) = TRIMPOT [part_number=maxDurationPoti package=trimpot_pth_s3_lock]
  R6_(100) = Resistor [tolerance=±5% resistance=100 package=THT]
  C2_(10u) = Tantalum Capacitor [capacitance=10µF package="100 mil [THT, tantalum]"]
  R7_(10k) = Resistor [tolerance=±5% resistance=10k package=THT]
  R8_(10k) = Resistor [tolerance=±5% resistance=10k package=THT]
  resetButton = Pushbutton [package="[THT]"]
  redLED = LED - 5mm [color="Red (633nm)" package="5 mm [THT]"]
  R9_(220) = Resistor [tolerance=±5% resistance=220 package=THT]
  SCT013 = female alternating pin header, 2 pins [form="♀ (female)"]
  Nano_Power = female pin header, 2 pins [form="♀ (female)"]
  J4 = female pin header, 5 pins [form="♀ (female)"]
  greenLED_(Amps_above_thresh) = LED - 5mm [color="Green (555nm)" package="5 mm [THT]"]
  R10_(220) = Resistor [tolerance=±5% resistance=220 package=THT]

nets:
  N1: Arduino_Nano.GND, SSR.-, durationExtensionPot_(0-300s).CCW, ampsThresholdPoti_(0-30A).CCW, maxDurationPoti_(0-1h).CCW, C2_(10u).-, R8_(10k).Pin_1, resetButton.Pin_3, resetButton.Pin_4, redLED.cathode, Nano_Power.pin2, J4.pin1, greenLED_(Amps_above_thresh).cathode
  N2: Arduino_Nano.D2, resetButton.Pin_1, resetButton.Pin_2, J4.pin2
  N3: Arduino_Nano.D4, R9_(220).Pin_1
  N4: Arduino_Nano.D7, SSR.+, J4.pin4
  N5: Arduino_Nano.D8, R10_(220).Pin_1
  N6: Arduino_Nano.VIN, Nano_Power.pin1
  N7: Arduino_Nano.5V, durationExtensionPot_(0-300s).CW, ampsThresholdPoti_(0-30A).CW, maxDurationPoti_(0-1h).CW, R7_(10k).Pin_0
  N8: Arduino_Nano.A7, R6_(100).Pin_0, SCT013.pin1
  N9: Arduino_Nano.A2, durationExtensionPot_(0-300s).WIPER
  N10: Arduino_Nano.A1, ampsThresholdPoti_(0-30A).WIPER
  N11: Arduino_Nano.A0, maxDurationPoti_(0-1h).WIPER
  N12: R6_(100).Pin_1, C2_(10u).+, R7_(10k).Pin_1, R8_(10k).Pin_0, SCT013.pin2
  N13: redLED.anode, R9_(220).Pin_0, J4.pin3
  N14: J4.pin5, greenLED_(Amps_above_thresh).anode, R10_(220).Pin_0
